// Logisim project single_cycle_RISC v.circ as structural Verilog: 9 circuits, main circuit main
module Alu (
  input  in_1,
  input  [31:0] in_2,
  input  [31:0] in_3,
  input  [2:0] in_4,
  input  in_5,
  output [31:0] out_6
);

  wire and_2_out, and_3_out, comparator_1_eq, comparator_1_gt, comparator_1_lt, comparator_2_eq,
       comparator_2_gt, comparator_2_lt, or_2_out, or_3_out;
  wire [31:0] adder_1_out, and_1_out, bit_extender_1_out, bit_extender_2_out, multiplexer_1_out,
       multiplexer_2_out, or_1_out, shifter_1_out, shifter_2_out, shifter_3_out, subtractor_1_out, xor_1_out;

  assign or_1_out = in_2 | in_3;  // OR_Gate or_1, 32 bits wide
  assign and_1_out = in_2 & in_3;  // AND_Gate and_1, 32 bits wide
  Adder #(.width(32)) adder_1 (.a(in_2), .b(in_3), .out(adder_1_out));  // open: cin, cout
  Multiplexer #(.width(32), .enable("false")) multiplexer_1 (
    .in0(adder_1_out), .in1(subtractor_1_out), .out(multiplexer_1_out), .sel(in_1));
  Subtractor #(.width(32)) subtractor_1 (.a(in_2), .b(in_3), .out(subtractor_1_out));  // open: bin, bout
  Shifter #(.width(32)) shifter_1 (.in(in_2), .\dist (in_3[4:0]), .out(shifter_1_out));
  and and_2 (and_2_out, comparator_1_gt, comparator_1_eq);
  Comparator #(.width(32)) comparator_1 (
    .a(in_2), .b(in_3), .gt(comparator_1_gt), .eq(comparator_1_eq), .lt(comparator_1_lt));
  or or_2 (or_2_out, comparator_1_lt, comparator_1_lt);
  Comparator #(.width(32), .mode("unsigned")) comparator_2 (
    .a(in_2), .b(in_3), .gt(comparator_2_gt), .eq(comparator_2_eq), .lt(comparator_2_lt));
  or or_3 (or_3_out, comparator_2_gt, comparator_2_lt);
  assign xor_1_out = in_2 ^ in_3;  // XOR_Gate xor_1, 32 bits wide
  and and_3 (and_3_out, comparator_2_eq, comparator_2_lt);
  Shifter #(.width(32), .shift("lr")) shifter_2 (.in(in_2), .\dist (in_3[4:0]), .out(shifter_2_out));
  Shifter #(.width(32), .shift("ar")) shifter_3 (.in(in_2), .\dist (in_3[4:0]), .out(shifter_3_out));
  assign bit_extender_1_out = {{31{1'b0}}, or_2_out};  // Bit_Extender bit_extender_1
  assign bit_extender_2_out = {{31{1'b0}}, or_3_out};  // Bit_Extender bit_extender_2
  Multiplexer #(.width(32), .enable("false")) multiplexer_2 (
    .in0(shifter_2_out), .in1(shifter_3_out), .out(multiplexer_2_out), .sel(in_1));
  Multiplexer #(.select(3), .width(32)) multiplexer_3 (
    .in0(multiplexer_1_out), .in1(shifter_1_out), .in2(bit_extender_1_out), .in3(bit_extender_2_out),
    .in4(xor_1_out), .in5(multiplexer_2_out), .in6(or_1_out), .in7(and_1_out), .out(out_6), .sel(in_4),
    .en(in_5));

  // Notes on the sheet:
  //   add
  //   sub
  //   sll
  //   slt
  //   sltu
  //   xor
  //   srl
  //   or
  //   and
  //   sra
  //   R,I-type
endmodule

module main (
  input  in_1,
  input  in_2,
  output [31:0] out_3,
  output [31:0] out_4,
  output [31:0] out_5,
  output [31:0] out_6,
  output [31:0] out_7,
  output [31:0] out_8
);

  wire and_1_out, bit_extender_1_out, clock_1_out, control_unit_1_branch, control_unit_1_load,
       control_unit_1_reg_write, control_unit_1_sel_opernd_b, control_unit_1_store, decoder_1_func7,
       multiplexer_13_out, opcode_identifier_1_auipc, opcode_identifier_1_jalr, opcode_identifier_1_lui,
       opcode_identifier_1_out_2, opcode_identifier_1_out_3, opcode_identifier_1_out_5,
       opcode_identifier_1_uj_type, or_1_out;
  wire [2:0] decoder_1_out_8;
  wire [4:0] decoder_1_rd, decoder_1_rs1, decoder_1_rs2, multiplexer_7_out, multiplexer_8_out,
       multiplexer_10_out;
  wire [6:0] decoder_1_opcode;
  wire [31:0] adder_1_out, adder_2_out, adder_3_out, adder_4_out, adder_5_out, adder_6_out,
       immediate_identifier_1_out_2, immediate_identifier_1_out_3, immediate_identifier_1_out_4,
       immediate_identifier_1_out_5, immediate_identifier_1_out_6, multiplexer_1_out, multiplexer_2_out,
       multiplexer_3_out, multiplexer_4_out, multiplexer_5_out, multiplexer_6_out, multiplexer_9_out,
       multiplexer_11_out, multiplexer_14_out, ram_2_data, register_1_q, shifter_1_out, shifter_2_out;

  Clock clock_1 (.out(clock_1_out));
  Shifter #(.width(32)) shifter_1 (.in(immediate_identifier_1_out_4), .\dist ({5{1'b0}}), .out(shifter_1_out));
  Adder #(.width(32)) adder_1 (.a(shifter_1_out), .b(register_1_q), .out(adder_1_out));  // open: cin, cout
  Multiplexer #(.width(32), .enable("false")) multiplexer_1 (
    .in0(adder_4_out), .in1(adder_1_out), .out(multiplexer_1_out), .sel(and_1_out));
  Shifter #(.width(32)) shifter_2 (.in(immediate_identifier_1_out_6), .\dist ({5{1'b0}}), .out(shifter_2_out));
  Adder #(.width(32)) adder_2 (.a(register_1_q), .b(shifter_2_out), .out(adder_2_out));  // open: cin, cout
  Multiplexer #(.width(32), .enable("false")) multiplexer_2 (
    .in0(multiplexer_1_out), .in1(adder_2_out), .out(multiplexer_2_out), .sel(opcode_identifier_1_uj_type));
  Bit_Extender #(.in_width(32), .out_width(1)) bit_extender_1 (.in(out_7), .out(bit_extender_1_out));
  // Probe on out_7
  Multiplexer #(.width(32), .enable("false")) multiplexer_3 (
    .in0(multiplexer_2_out), .in1(adder_3_out), .out(multiplexer_3_out), .sel(opcode_identifier_1_jalr));
  Adder #(.width(32)) adder_3 (.a(immediate_identifier_1_out_2), .b(out_3), .out(adder_3_out));  // open: cin, cout
  and and_1 (and_1_out, bit_extender_1_out, control_unit_1_branch);
  Register #(.width(32)) register_1 (
    .D(multiplexer_3_out), .Q(register_1_q), .clk(clock_1_out), .clr(in_1));  // open: en
  // Probe on decoder_1_out_8
  Adder #(.width(32)) adder_4 (.a(register_1_q), .b(32'h4), .out(adder_4_out));  // open: cin, cout
  RAM #(.addrWidth(24), .dataWidth(32)) ram_1 (
    .addr(register_1_q[25:2]), .data(out_6), .sel(in_2));  // open: clk, ld, clr
  // Probe on out_5
  decoder decoder_1 (
    .in_1(out_6), .opcode(decoder_1_opcode), .rd(decoder_1_rd), .rs1(decoder_1_rs1), .rs2(decoder_1_rs2),
    .func7(decoder_1_func7), .out_8(decoder_1_out_8), .in_2(opcode_identifier_1_out_5));
  // Probe on register_1_q
  opcode_identifier opcode_identifier_1 (
    .in_1(decoder_1_opcode), .out_2(opcode_identifier_1_out_2), .out_3(opcode_identifier_1_out_3),
    .out_5(opcode_identifier_1_out_5), .auipc(opcode_identifier_1_auipc),
    .UJ_type(opcode_identifier_1_uj_type), .lui(opcode_identifier_1_lui), .jalr(opcode_identifier_1_jalr));  // open: S_type, load
  // Probe on decoder_1_rs1
  Multiplexer #(.width(32), .enable("false")) multiplexer_4 (
    .in0(out_5), .in1(ram_2_data), .out(multiplexer_4_out), .sel(control_unit_1_load));
  // Probe on decoder_1_rs2
  control_unit control_unit_1 (
    .in_1(decoder_1_opcode), .sel_opernd_B(control_unit_1_sel_opernd_b), .branch(control_unit_1_branch),
    .reg_write(control_unit_1_reg_write), .store(control_unit_1_store), .load(control_unit_1_load));
  Adder #(.width(32)) adder_5 (
    .a(register_1_q), .b(immediate_identifier_1_out_5), .out(adder_5_out));  // open: cin, cout
  Multiplexer #(.width(32), .enable("false")) multiplexer_5 (
    .in0(multiplexer_4_out), .in1(adder_4_out), .out(multiplexer_5_out), .sel(opcode_identifier_1_uj_type));
  Multiplexer #(.width(32), .enable("false")) multiplexer_6 (
    .in0(multiplexer_5_out), .in1(adder_4_out), .out(multiplexer_6_out), .sel(opcode_identifier_1_jalr));
  // Probe on multiplexer_10_out
  Multiplexer #(.width(5), .enable("false")) multiplexer_7 (
    .in0(decoder_1_rd), .in1(5'b00001), .out(multiplexer_7_out), .sel(opcode_identifier_1_uj_type));
  Multiplexer #(.width(5), .enable("false")) multiplexer_8 (
    .in0(multiplexer_7_out), .in1(decoder_1_rd), .out(multiplexer_8_out), .sel(opcode_identifier_1_jalr));
  Multiplexer #(.width(32), .enable("false")) multiplexer_9 (
    .in0(multiplexer_6_out), .in1(adder_5_out), .out(multiplexer_9_out), .sel(opcode_identifier_1_auipc));
  Multiplexer #(.width(5), .enable("false")) multiplexer_10 (
    .in0(multiplexer_8_out), .in1(decoder_1_rd), .out(multiplexer_10_out), .sel(opcode_identifier_1_auipc));
  immediate_identifier immediate_identifier_1 (
    .in_1(out_6), .out_2(immediate_identifier_1_out_2), .out_3(immediate_identifier_1_out_3),
    .out_4(immediate_identifier_1_out_4), .out_5(immediate_identifier_1_out_5),
    .out_6(immediate_identifier_1_out_6));
  Multiplexer #(.width(32), .enable("false")) multiplexer_11 (
    .in0(multiplexer_9_out), .in1(immediate_identifier_1_out_5), .out(multiplexer_11_out),
    .sel(opcode_identifier_1_lui));
  reg_file reg_file_1 (
    .in_1(decoder_1_rs1), .write_data(control_unit_1_reg_write), .rd(multiplexer_10_out), .clk(clock_1_out),
    .in_5(multiplexer_11_out), .rs2(decoder_1_rs2), .out_7(out_3), .out_8(out_4));
  // Probe on out_4
  // Probe on immediate_identifier_1_out_2
  // Probe on immediate_identifier_1_out_4
  // Probe on out_3
  // Probe on out_8
  Multiplexer #(.width(32), .enable("false")) multiplexer_12 (
    .in0(out_4), .in1(immediate_identifier_1_out_2), .out(out_8), .sel(control_unit_1_sel_opernd_b));
  // Probe on immediate_identifier_1_out_6
  // Probe on out_3
  // Probe on out_8
  Alu alu_1 (
    .in_1(decoder_1_func7), .in_2(out_3), .in_3(out_8), .in_4(decoder_1_out_8), .out_6(out_5),
    .in_5(multiplexer_13_out));
  Multiplexer #(.enable("false")) multiplexer_13 (
    .in0(opcode_identifier_1_out_2), .in1(opcode_identifier_1_out_5), .out(multiplexer_13_out),
    .sel(opcode_identifier_1_out_5));
  // Probe on out_5
  // Probe on out_4
  // Probe on decoder_1_out_8
  // Probe on out_3
  Multiplexer #(.width(32), .enable("false")) multiplexer_14 (
    .in0(immediate_identifier_1_out_3), .in1(immediate_identifier_1_out_2), .out(multiplexer_14_out),
    .sel(control_unit_1_load));
  // Probe on out_4
  branch branch_1 (
    .in_1(out_3), .in_2(out_4), .function_3(decoder_1_out_8), .out_5(out_7), .in_3(opcode_identifier_1_out_3));
  // Probe on multiplexer_14_out
  Adder #(.width(32)) adder_6 (.a(multiplexer_14_out), .b(out_3), .out(adder_6_out));  // open: cin, cout
  // Probe on adder_6_out
  // Probe on ram_2_data
  // Probe on out_7
  RAM #(.addrWidth(24), .dataWidth(32), .bus("separate")) ram_2 (
    .addr(adder_6_out[23:0]), .din(out_4), .data(ram_2_data), .str(control_unit_1_store), .sel(or_1_out),
    .clk(clock_1_out), .ld(control_unit_1_load));  // open: clr
  or or_1 (or_1_out, control_unit_1_store, control_unit_1_load);

  // Notes on the sheet:
  //   Program counter
  //   instruction memory
endmodule

module reg_file (
  input  [4:0] in_1,
  input  write_data,
  input  [4:0] rd,
  input  clk,
  input  [31:0] in_5,
  input  [4:0] rs2,
  output [31:0] out_7,
  output [31:0] out_8
);

  wire decoder_1_out0, decoder_1_out1, decoder_1_out2, decoder_1_out3, decoder_1_out4, decoder_1_out5,
       decoder_1_out6, decoder_1_out7, decoder_1_out8, decoder_1_out9, decoder_1_out10, decoder_1_out11,
       decoder_1_out12, decoder_1_out13, decoder_1_out14, decoder_1_out15, decoder_1_out16, decoder_1_out17,
       decoder_1_out18, decoder_1_out19, decoder_1_out20, decoder_1_out21, decoder_1_out22, decoder_1_out23,
       decoder_1_out24, decoder_1_out25, decoder_1_out26, decoder_1_out27, decoder_1_out28, decoder_1_out29,
       decoder_1_out30, decoder_1_out31;
  wire [31:0] register_1_q, register_2_q, register_3_q, register_4_q, register_5_q, register_6_q,
       register_7_q, register_8_q, register_9_q, register_10_q, register_11_q, register_12_q, register_13_q,
       register_14_q, register_15_q, register_16_q, register_17_q, register_18_q, register_19_q,
       register_20_q, register_21_q, register_22_q, register_23_q, register_24_q, register_25_q,
       register_26_q, register_27_q, register_28_q, register_29_q, register_30_q, register_31_q,
       register_32_q;

  Decoder #(.select(5)) decoder_1 (
    .out0(decoder_1_out0), .out1(decoder_1_out1), .out2(decoder_1_out2), .out3(decoder_1_out3),
    .out4(decoder_1_out4), .out5(decoder_1_out5), .out6(decoder_1_out6), .out7(decoder_1_out7),
    .out8(decoder_1_out8), .out9(decoder_1_out9), .out10(decoder_1_out10), .out11(decoder_1_out11),
    .out12(decoder_1_out12), .out13(decoder_1_out13), .out14(decoder_1_out14), .out15(decoder_1_out15),
    .out16(decoder_1_out16), .out17(decoder_1_out17), .out18(decoder_1_out18), .out19(decoder_1_out19),
    .out20(decoder_1_out20), .out21(decoder_1_out21), .out22(decoder_1_out22), .out23(decoder_1_out23),
    .out24(decoder_1_out24), .out25(decoder_1_out25), .out26(decoder_1_out26), .out27(decoder_1_out27),
    .out28(decoder_1_out28), .out29(decoder_1_out29), .out30(decoder_1_out30), .out31(decoder_1_out31),
    .sel(rd), .en(write_data));
  Register #(.width(32)) register_1 (.D({32{1'b0}}), .en(decoder_1_out0), .Q(register_1_q), .clk(clk), .clr(1'b0));
  Register #(.width(32)) register_2 (.D(in_5), .en(decoder_1_out1), .Q(register_2_q), .clk(clk), .clr(1'b0));
  Register #(.width(32)) register_3 (.D(in_5), .en(decoder_1_out2), .Q(register_3_q), .clk(clk), .clr(1'b0));
  Register #(.width(32)) register_4 (.D(in_5), .en(decoder_1_out3), .Q(register_4_q), .clk(clk), .clr(1'b0));
  Register #(.width(32)) register_5 (.D(in_5), .en(decoder_1_out4), .Q(register_5_q), .clk(clk), .clr(1'b0));
  Register #(.width(32)) register_6 (.D(in_5), .en(decoder_1_out5), .Q(register_6_q), .clk(clk), .clr(1'b0));
  Register #(.width(32)) register_7 (.D(in_5), .en(decoder_1_out6), .Q(register_7_q), .clk(clk), .clr(1'b0));
  Register #(.width(32)) register_8 (.D(in_5), .en(decoder_1_out7), .Q(register_8_q), .clk(clk), .clr(1'b0));
  Register #(.width(32)) register_9 (.D(in_5), .en(decoder_1_out8), .Q(register_9_q), .clk(clk), .clr(1'b0));
  Register #(.width(32)) register_10 (.D(in_5), .en(decoder_1_out9), .Q(register_10_q), .clk(clk), .clr(1'b0));
  Register #(.width(32)) register_11 (.D(in_5), .en(decoder_1_out10), .Q(register_11_q), .clk(clk), .clr(1'b0));
  Register #(.width(32)) register_12 (.D(in_5), .en(decoder_1_out11), .Q(register_12_q), .clk(clk), .clr(1'b0));
  Register #(.width(32)) register_13 (.D(in_5), .en(decoder_1_out12), .Q(register_13_q), .clk(clk), .clr(1'b0));
  Register #(.width(32)) register_14 (.D(in_5), .en(decoder_1_out13), .Q(register_14_q), .clk(clk), .clr(1'b0));
  Register #(.width(32)) register_15 (.D(in_5), .en(decoder_1_out14), .Q(register_15_q), .clk(clk), .clr(1'b0));
  Register #(.width(32)) register_16 (.D(in_5), .en(decoder_1_out15), .Q(register_16_q), .clk(clk), .clr(1'b0));
  Register #(.width(32)) register_17 (.D(in_5), .en(decoder_1_out16), .Q(register_17_q), .clk(clk), .clr(1'b0));
  Register #(.width(32)) register_18 (.D(in_5), .en(decoder_1_out17), .Q(register_18_q), .clk(clk), .clr(1'b0));
  Register #(.width(32)) register_19 (.D(in_5), .en(decoder_1_out18), .Q(register_19_q), .clk(clk), .clr(1'b0));
  Register #(.width(32)) register_20 (.D(in_5), .en(decoder_1_out19), .Q(register_20_q), .clk(clk), .clr(1'b0));
  Register #(.width(32)) register_21 (.D(in_5), .en(decoder_1_out20), .Q(register_21_q), .clk(clk), .clr(1'b0));
  Register #(.width(32)) register_22 (.D(in_5), .en(decoder_1_out21), .Q(register_22_q), .clk(clk), .clr(1'b0));
  Register #(.width(32)) register_23 (.D(in_5), .en(decoder_1_out22), .Q(register_23_q), .clk(clk), .clr(1'b0));
  Register #(.width(32)) register_24 (.D(in_5), .en(decoder_1_out23), .Q(register_24_q), .clk(clk), .clr(1'b0));
  Register #(.width(32)) register_25 (.D(in_5), .en(decoder_1_out24), .Q(register_25_q), .clk(clk), .clr(1'b0));
  Register #(.width(32)) register_26 (.D(in_5), .en(decoder_1_out25), .Q(register_26_q), .clk(clk), .clr(1'b0));
  Register #(.width(32)) register_27 (.D(in_5), .en(decoder_1_out26), .Q(register_27_q), .clk(clk), .clr(1'b0));
  Register #(.width(32)) register_28 (.D(in_5), .en(decoder_1_out27), .Q(register_28_q), .clk(clk), .clr(1'b0));
  Register #(.width(32)) register_29 (.D(in_5), .en(decoder_1_out28), .Q(register_29_q), .clk(clk), .clr(1'b0));
  Register #(.width(32)) register_30 (.D(in_5), .en(decoder_1_out29), .Q(register_30_q), .clk(clk), .clr(1'b0));
  Register #(.width(32)) register_31 (.D(in_5), .en(decoder_1_out30), .Q(register_31_q), .clk(clk), .clr(1'b0));
  Register #(.width(32)) register_32 (.D(in_5), .en(decoder_1_out31), .Q(register_32_q), .clr(1'b0));  // open: clk
  Multiplexer #(.select(5), .width(32), .enable("false")) multiplexer_1 (
    .in0(register_1_q), .in1(register_2_q), .in2(register_3_q), .in3(register_4_q), .in4(register_5_q),
    .in5(register_6_q), .in6(register_7_q), .in7(register_8_q), .in8(register_9_q), .in9(register_10_q),
    .in10(register_11_q), .in11(register_12_q), .in12(register_13_q), .in13(register_14_q),
    .in14(register_15_q), .in15(register_16_q), .in16(register_17_q), .in17(register_18_q),
    .in18(register_19_q), .in19(register_20_q), .in20(register_21_q), .in21(register_22_q),
    .in22(register_23_q), .in23(register_24_q), .in24(register_25_q), .in25(register_26_q),
    .in26(register_27_q), .in27(register_28_q), .in28(register_29_q), .in29(register_30_q),
    .in30(register_31_q), .in31(register_32_q), .out(out_7), .sel(in_1));
  Multiplexer #(.select(5), .width(32), .enable("false")) multiplexer_2 (
    .in0(register_1_q), .in1(register_2_q), .in2(register_3_q), .in3(register_4_q), .in4(register_5_q),
    .in5(register_6_q), .in6(register_7_q), .in7(register_8_q), .in8(register_9_q), .in9(register_10_q),
    .in10(register_11_q), .in11(register_12_q), .in12(register_13_q), .in13(register_14_q),
    .in14(register_15_q), .in15(register_16_q), .in16(register_17_q), .in17(register_18_q),
    .in18(register_19_q), .in19(register_20_q), .in20(register_21_q), .in21(register_22_q),
    .in22(register_23_q), .in23(register_24_q), .in24(register_25_q), .in25(register_26_q),
    .in26(register_27_q), .in27(register_28_q), .in28(register_29_q), .in29(register_30_q),
    .in30(register_31_q), .in31(register_32_q), .out(out_8), .sel(rs2));

  // Notes on the sheet:
  //   rs1
  //   read_d1
  //   read_d2
endmodule

module decoder (
  input  [31:0] in_1,
  input  in_2,
  output [6:0] opcode,
  output [4:0] rd,
  output [4:0] rs1,
  output func7,
  output [4:0] rs2,
  output [2:0] out_8
);

  wire comparator_1_eq, comparator_2_eq, comparator_3_eq, comparator_4_eq, comparator_5_eq, comparator_6_eq,
       comparator_7_eq, comparator_8_eq, comparator_9_eq, comparator_10_eq, comparator_11_eq,
       priority_encoder_1_en_out;
  wire [2:0] multiplexer_2_out, priority_encoder_1_out, priority_encoder_2_out, priority_encoder_3_out;

  Multiplexer #(.enable("false")) multiplexer_1 (.in0(in_1[30]), .in1(1'b0), .out(func7), .sel(in_2));
  Comparator #(.width(3)) comparator_1 (.a(in_1[14:12]), .b(3'b000), .eq(comparator_1_eq));  // open: gt, lt
  Comparator #(.width(3)) comparator_2 (.a(in_1[14:12]), .b(3'b001), .eq(comparator_2_eq));  // open: gt, lt
  Comparator #(.width(3)) comparator_3 (.a(in_1[14:12]), .b(3'b010), .eq(comparator_3_eq));  // open: gt, lt
  Comparator #(.width(3)) comparator_4 (.a(in_1[14:12]), .b(3'b011), .eq(comparator_4_eq));  // open: gt, lt
  Comparator #(.width(3)) comparator_5 (.a(in_1[14:12]), .b(3'b100), .eq(comparator_5_eq));  // open: gt, lt
  Comparator #(.width(3)) comparator_6 (.a(in_1[14:12]), .b(3'b101), .eq(comparator_6_eq));  // open: gt, lt
  Comparator #(.width(3)) comparator_7 (.a(in_1[14:12]), .b(3'b110), .eq(comparator_7_eq));  // open: gt, lt
  Comparator #(.width(3)) comparator_8 (.a(in_1[14:12]), .b(3'b111), .eq(comparator_8_eq));  // open: gt, lt
  Comparator #(.width(7)) comparator_9 (.a(in_1[6:0]), .b(7'b0110011), .eq(comparator_9_eq));  // open: gt, lt
  Priority_Encoder priority_encoder_1 (
    .in0(comparator_1_eq), .in1(comparator_2_eq), .in2(comparator_3_eq), .in3(comparator_4_eq),
    .in4(comparator_5_eq), .in5(comparator_6_eq), .in6(comparator_7_eq), .in7(comparator_8_eq),
    .out(priority_encoder_1_out), .en_in(comparator_9_eq), .en_out(priority_encoder_1_en_out));  // open: gs
  // Probe on priority_encoder_1_out
  Comparator #(.width(7)) comparator_10 (.a(in_1[6:0]), .b(7'b0010011), .eq(comparator_10_eq));  // open: gt, lt
  Priority_Encoder priority_encoder_2 (
    .in0(comparator_1_eq), .in1(comparator_2_eq), .in2(comparator_3_eq), .in3(comparator_4_eq),
    .in4(comparator_5_eq), .in5(comparator_6_eq), .in6(comparator_7_eq), .in7(comparator_8_eq),
    .out(priority_encoder_2_out), .en_in(comparator_10_eq));  // open: gs, en_out
  // Probe on priority_encoder_2_out
  Comparator #(.width(7)) comparator_11 (.a(in_1[6:0]), .b(7'b1100011), .eq(comparator_11_eq));  // open: gt, lt
  Priority_Encoder priority_encoder_3 (
    .in0(comparator_1_eq), .in1(comparator_2_eq), .in2(comparator_3_eq), .in3(comparator_4_eq),
    .in4(comparator_5_eq), .in5(comparator_6_eq), .in6(comparator_7_eq), .in7(comparator_8_eq),
    .out(priority_encoder_3_out), .en_in(comparator_11_eq));  // open: gs, en_out
  Multiplexer #(.width(3), .enable("false")) multiplexer_2 (
    .in0(priority_encoder_1_out), .in1(priority_encoder_2_out), .out(multiplexer_2_out),
    .sel(comparator_10_eq));
  // Probe on priority_encoder_3_out
  // Probe on multiplexer_2_out
  Multiplexer #(.width(3), .enable("false")) multiplexer_3 (
    .in0(multiplexer_2_out), .in1(priority_encoder_3_out), .out(out_8), .sel(comparator_11_eq));

  assign opcode = in_1[6:0];
  assign rd = in_1[11:7];
  assign rs1 = in_1[19:15];
  assign rs2 = in_1[24:20];

  // Notes on the sheet:
  //   R-type
  //   func3
endmodule

module opcode_identifier (
  input  [6:0] in_1,
  output out_2,
  output out_3,
  output load,
  output out_5,
  output jalr,
  output auipc,
  output lui,
  output S_type,
  output UJ_type
);

  wire comparator_1_eq, comparator_2_eq, comparator_4_eq, comparator_6_eq, comparator_8_eq;

  Comparator #(.width(7), .mode("unsigned")) comparator_1 (
    .a(in_1), .b(7'b0111011), .eq(comparator_1_eq));  // open: gt, lt
  // Probe on 7'b0111011
  Comparator #(.width(7)) comparator_2 (.a(in_1), .b(7'b0110011), .eq(comparator_2_eq));  // open: gt, lt
  // Probe on 7'b0110011
  Comparator #(.width(7), .mode("unsigned")) comparator_3 (.a(in_1), .b(7'b1100011), .eq(out_3));  // open: gt, lt
  // Probe on 7'b1100011
  Comparator #(.width(7), .mode("unsigned")) comparator_4 (
    .a(in_1), .b(7'b0010011), .eq(comparator_4_eq));  // open: gt, lt
  // Probe on 7'b0010011
  Comparator #(.width(7), .mode("unsigned")) comparator_5 (.a(in_1), .b(7'b0000011), .eq(load));  // open: gt, lt
  // Probe on 7'b0000011
  Comparator #(.width(7), .mode("unsigned")) comparator_6 (
    .a(in_1), .b(7'b0011011), .eq(comparator_6_eq));  // open: gt, lt
  // Probe on 7'b0011011
  Comparator #(.width(7), .mode("unsigned")) comparator_7 (.a(in_1), .b(7'b1100111), .eq(jalr));  // open: gt, lt
  // Probe on 7'b1100111
  Comparator #(.width(7), .mode("unsigned")) comparator_8 (
    .a(in_1), .b(7'b1110011), .eq(comparator_8_eq));  // open: gt, lt
  // Probe on 7'b1110011
  Comparator #(.width(7), .mode("unsigned")) comparator_9 (.a(in_1), .b(7'b0010111), .eq(auipc));  // open: gt, lt
  // Probe on 7'b0010111
  Comparator #(.width(7), .mode("unsigned")) comparator_10 (.a(in_1), .b(7'b0110111), .eq(lui));  // open: gt, lt
  // Probe on 7'b0110111
  Comparator #(.width(7), .mode("unsigned")) comparator_11 (.a(in_1), .b(7'b0100011), .eq(S_type));  // open: gt, lt
  // Probe on 7'b0100011
  Comparator #(.width(7), .mode("unsigned")) comparator_12 (.a(in_1), .b(7'b1101111), .eq(UJ_type));  // open: gt, lt
  // Probe on 7'b1101111
  or or_1 (out_2, comparator_1_eq, comparator_2_eq);
  or or_2 (out_5, comparator_4_eq, load, comparator_6_eq, jalr, comparator_8_eq);

  // Notes on the sheet:
  //   R-type
  //   SB-type
  //   I-type
endmodule

module immediate_identifier (
  input  [31:0] in_1,
  output [31:0] out_2,
  output [31:0] out_3,
  output [31:0] out_4,
  output [31:0] out_5,
  output [31:0] out_6
);

  // Probe on in_1[30]
  assign out_3 = {{20{in_1[31]}}, {in_1[31:25], in_1[11:7]}};  // Bit_Extender bit_extender_1
  assign out_4 = {{19{in_1[31]}}, {in_1[31], in_1[7], in_1[30:25], in_1[11:8], 1'b0}};  // Bit_Extender bit_extender_2
  // Probe on in_1[31:12]
  // Probe on {in_1[31], in_1[19:12], in_1[20], in_1[30:21], 1'b0}
  assign out_6 = {{11{in_1[31]}}, {in_1[31], in_1[19:12], in_1[20], in_1[30:21], 1'b0}};  // Bit_Extender bit_extender_3
  assign out_2 = {{20{in_1[31]}}, in_1[31:20]};  // Bit_Extender bit_extender_4
  // Probe on {in_1[31:25], in_1[11:7]}
  // Probe on {in_1[31], in_1[7], in_1[30:25], in_1[11:8], 1'b0}
  // Probe on out_2
  // Probe on out_3
  // Probe on out_4
  // Probe on {in_1[31:12], {12{1'b0}}}
  // Probe on out_6

  assign out_5 = {in_1[31:12], {12{1'b0}}};

  // Notes on the sheet:
  //   function 7
  //   I-type
  //   S-type
  //   SB-type
  //   U-type
  //   UJ-type
  //   immediate
  //   immediate
  //   immediate
  //   immediate
  //   immediate
endmodule

module branch (
  input  [31:0] in_1,
  input  [31:0] in_2,
  input  in_3,
  input  [2:0] function_3,
  output [31:0] out_5
);

  wire comparator_1_eq, comparator_2_gt, comparator_2_lt, comparator_3_lt, comparator_4_eq, comparator_4_gt,
       comparator_5_lt, comparator_6_eq, comparator_6_gt, or_1_out, or_2_out, or_3_out;
  wire [31:0] bit_extender_1_out, bit_extender_2_out, bit_extender_3_out, bit_extender_4_out,
       bit_extender_5_out, bit_extender_6_out;

  assign bit_extender_1_out = {{31{1'b0}}, comparator_1_eq};  // Bit_Extender bit_extender_1
  Comparator #(.width(32)) comparator_1 (.a(in_1), .b(in_2), .eq(comparator_1_eq));  // open: gt, lt
  or or_1 (or_1_out, comparator_2_gt, comparator_2_lt);
  Comparator #(.width(32)) comparator_2 (.a(in_1), .b(in_2), .gt(comparator_2_gt), .lt(comparator_2_lt));  // open: eq
  Comparator #(.width(32)) comparator_3 (.a(in_1), .b(in_2), .lt(comparator_3_lt));  // open: gt, eq
  assign bit_extender_2_out = {{31{1'b0}}, comparator_3_lt};  // Bit_Extender bit_extender_2
  or or_2 (or_2_out, comparator_4_gt, comparator_4_eq);
  Comparator #(.width(32)) comparator_4 (.a(in_1), .b(in_2), .gt(comparator_4_gt), .eq(comparator_4_eq));  // open: lt
  Comparator #(.width(32), .mode("unsigned")) comparator_5 (.a(in_1), .b(in_2), .lt(comparator_5_lt));  // open: gt, eq
  assign bit_extender_3_out = {{31{1'b0}}, comparator_5_lt};  // Bit_Extender bit_extender_3
  or or_3 (or_3_out, comparator_6_gt, comparator_6_eq);
  Comparator #(.width(32), .mode("unsigned")) comparator_6 (
    .a(in_1), .b(in_2), .gt(comparator_6_gt), .eq(comparator_6_eq));  // open: lt
  assign bit_extender_4_out = {{31{1'b0}}, or_1_out};  // Bit_Extender bit_extender_4
  assign bit_extender_5_out = {{31{1'b0}}, or_2_out};  // Bit_Extender bit_extender_5
  assign bit_extender_6_out = {{31{1'b0}}, or_3_out};  // Bit_Extender bit_extender_6
  Multiplexer #(.select(3), .width(32)) multiplexer_1 (
    .in0(bit_extender_1_out), .in1(bit_extender_4_out), .in4(bit_extender_2_out), .in5(bit_extender_5_out),
    .in6(bit_extender_3_out), .in7(bit_extender_6_out), .out(out_5), .sel(function_3), .en(in_3));  // open: in2, in3
  // Probe on out_5

  // Notes on the sheet:
  //   register 1
  //   register 2
  //   beq
  //   bne
  //   blt
  //   bge
  //   bltu
  //   bgeu
  //   SB-type
  //   RESULT
endmodule

module PC (
  input  in_1,
  input  in_2,
  output [31:0] out_3
);

  wire [31:0] adder_1_out, register_1_q;

  Register #(.width(32)) register_1 (.D(adder_1_out), .Q(register_1_q), .clk(in_2), .clr(in_1));  // open: en
  Adder #(.width(32)) adder_1 (.a(register_1_q), .b(32'h4), .out(adder_1_out));  // open: cin, cout
  RAM #(.addrWidth(24), .dataWidth(32)) ram_1 (.addr(register_1_q[25:2]), .data(out_3));  // open: sel, clk, ld, clr

  // Notes on the sheet:
  //   Program counter
  //   instruction memory
endmodule

module control_unit (
  input  [6:0] in_1,
  output sel_opernd_B,
  output branch,
  output reg_write,
  output store,
  output load
);

  wire opcode_identifier_1_jalr, opcode_identifier_1_lui, opcode_identifier_1_out_2,
       opcode_identifier_1_out_5, opcode_identifier_1_uj_type;

  opcode_identifier opcode_identifier_1 (
    .in_1(in_1), .out_2(opcode_identifier_1_out_2), .out_3(branch), .out_5(opcode_identifier_1_out_5),
    .S_type(store), .UJ_type(opcode_identifier_1_uj_type), .load(load), .lui(opcode_identifier_1_lui),
    .jalr(opcode_identifier_1_jalr));  // open: auipc
  or or_1 (sel_opernd_B, branch, opcode_identifier_1_out_5, store);
  or or_2 (reg_write, opcode_identifier_1_out_2, opcode_identifier_1_out_5, opcode_identifier_1_jalr, opcode_identifier_1_lui, opcode_identifier_1_uj_type);
endmodule
